// Logisim project DisplayDriverFinal.circ as structural Verilog: 1 circuit, main circuit display
module display (
  input  Mode,
  input  RST,
  input  DecSecs,
  input  IncSecs,
  input  DecMins,
  input  IncMins,
  input  DecHrs,
  input  IncHrs,
  output G0,
  output F0,
  output A0,
  output B0,
  output DP0,
  output C0,
  output E0,
  output D0,
  output A1,
  output F1,
  output G1,
  output B1,
  output G2,
  output D1,
  output C1,
  output E1,
  output F2,
  output A2,
  output B2,
  output C2,
  output D2,
  output E2,
  output G3,
  output F3,
  output A3,
  output B3,
  output C3,
  output D3,
  output E3,
  output F4,
  output A4,
  output G4,
  output B4,
  output C4,
  output E4,
  output D4,
  output F5,
  output A5,
  output B5,
  output G5,
  output C5,
  output D5,
  output E5
);

  wire and_2_out, and_3_out, and_4_out, and_5_out, and_6_out, and_7_out, and_8_out, and_9_out, and_10_out,
       and_11_out, and_12_out, and_13_out, clock_1_out, multiplexer_1_out, multiplexer_2_out,
       multiplexer_3_out, multiplexer_5_out, multiplexer_6_out, multiplexer_7_out, multiplexer_13_out,
       multiplexer_15_out, multiplexer_16_out, multiplexer_17_out, multiplexer_18_out, multiplexer_19_out,
       multiplexer_20_out, nor_1_out, nor_2_out, nor_3_out, nor_4_out, nor_5_out, nor_6_out, not_1_out,
       not_2_out, not_3_out, not_4_out, not_5_out, not_6_out, not_7_out, not_8_out, not_10_out, not_11_out,
       or_1_out, or_2_out, or_3_out, or_4_out, t_ff_1_q, t_ff_2_q, undriven, undriven_2, undriven_3,
       undriven_4;
  wire [2:0] counter_2_q, counter_6_q, multiplexer_10_out, multiplexer_12_out, multiplexer_14_out;
  wire [3:0] counter_1_q, counter_3_q, counter_4_q, counter_5_q, multiplexer_4_out, multiplexer_8_out,
       multiplexer_9_out, multiplexer_11_out;

  Clock clock_1 (.out(clock_1_out));
  and and_1 (DP0, clock_1_out, not_11_out);
  Multiplexer multiplexer_1 (.in0(IncSecs), .in1(not_1_out), .out(multiplexer_1_out), .sel(DecSecs));
  not not_1 (not_1_out, IncSecs);
  Multiplexer multiplexer_2 (.in0(IncMins), .in1(not_2_out), .out(multiplexer_2_out), .sel(DecMins));
  not not_2 (not_2_out, IncMins);
  Multiplexer multiplexer_3 (.in0(IncHrs), .in1(not_3_out), .out(multiplexer_3_out), .sel(DecHrs));
  not not_3 (not_3_out, IncHrs);
  Multiplexer #(.width(4)) multiplexer_4 (.in0(4'b1001), .in1(4'b0011), .out(multiplexer_4_out), .sel(nor_2_out));
  Multiplexer multiplexer_5 (.in0(multiplexer_1_out), .in1(clock_1_out), .out(multiplexer_5_out), .sel(not_11_out));
  Multiplexer multiplexer_6 (.in0(multiplexer_2_out), .in1(clock_1_out), .out(multiplexer_6_out), .sel(not_11_out));
  or or_1 (or_1_out, and_13_out, and_5_out, and_4_out);
  not not_4 (not_4_out, DecMins);
  Multiplexer multiplexer_7 (.in0(multiplexer_3_out), .in1(clock_1_out), .out(multiplexer_7_out), .sel(not_11_out));
  Multiplexer #(.width(4)) multiplexer_8 (
    .in0(4'b0000), .in1(multiplexer_4_out), .out(multiplexer_8_out), .sel(DecHrs));
  or or_2 (or_2_out, or_1_out, multiplexer_17_out);
  not not_5 (not_5_out, not_7_out);
  Multiplexer #(.width(4)) multiplexer_9 (.in0(4'b0000), .in1(4'b1001), .out(multiplexer_9_out), .sel(DecMins));
  Counter #(.max('hf), .width(4)) counter_1 (
    .clr(RST), .load(or_2_out), .up(not_6_out), .count(multiplexer_15_out), .clk(multiplexer_7_out),
    .D(multiplexer_8_out), .Q(counter_1_q));  // open: carry
  not not_6 (not_6_out, DecHrs);
  Counter #(.max('h7), .width(3)) counter_2 (
    .clr(RST), .load(or_1_out), .up(not_6_out), .count(or_2_out), .clk(multiplexer_7_out),
    .D(multiplexer_10_out), .Q(counter_2_q));  // open: carry
  Multiplexer #(.width(3)) multiplexer_10 (.in0(3'b000), .in1(3'b010), .out(multiplexer_10_out), .sel(and_5_out));
  Counter #(.max('hf), .width(4)) counter_3 (
    .clr(RST), .load(multiplexer_16_out), .up(not_7_out), .count(1'b1), .clk(multiplexer_5_out),
    .D(multiplexer_11_out), .Q(counter_3_q));  // open: carry
  not not_7 (not_7_out, DecSecs);
  Multiplexer #(.width(4)) multiplexer_11 (.in0(4'b0000), .in1(4'b1001), .out(multiplexer_11_out), .sel(DecSecs));
  Counter #(.max('hf), .width(4)) counter_4 (
    .clr(RST), .load(or_4_out), .up(not_7_out), .count(multiplexer_16_out), .clk(multiplexer_5_out),
    .D({1'b0, multiplexer_12_out}), .Q(counter_4_q));  // open: carry
  Multiplexer #(.width(3)) multiplexer_12 (.in0(3'b000), .in1(3'b101), .out(multiplexer_12_out), .sel(not_5_out));
  Multiplexer multiplexer_13 (.in0(1'b1), .in1(and_10_out), .out(multiplexer_13_out), .sel(not_11_out));
  Counter #(.max('hf), .width(4)) counter_5 (
    .clr(RST), .load(multiplexer_18_out), .up(not_4_out), .count(multiplexer_13_out),
    .clk(multiplexer_6_out), .D(multiplexer_9_out), .Q(counter_5_q));  // open: carry
  Counter #(.max('h7), .width(3)) counter_6 (
    .clr(RST), .load(or_3_out), .up(not_4_out), .count(multiplexer_18_out), .clk(multiplexer_6_out),
    .D(multiplexer_14_out), .Q(counter_6_q));  // open: carry
  Multiplexer #(.width(3)) multiplexer_14 (.in0(3'b000), .in1(3'b101), .out(multiplexer_14_out), .sel(not_8_out));
  not not_8 (not_8_out, not_4_out);
  or or_3 (or_3_out, and_7_out, and_3_out);
  Multiplexer multiplexer_15 (.in0(1'b1), .in1(and_7_out), .out(multiplexer_15_out), .sel(not_11_out));
  T_Flip_Flop t_ff_1 (.T(undriven), .clk(undriven), .Q(t_ff_1_q));  // open: Qn, reset, preset
  Multiplexer multiplexer_16 (.in0(and_9_out), .in1(nor_5_out), .out(multiplexer_16_out), .sel(DecSecs));
  or or_4 (or_4_out, and_10_out, and_2_out);
  Multiplexer multiplexer_17 (.in0(and_8_out), .in1(nor_1_out), .out(multiplexer_17_out), .sel(DecHrs));
  // NOT_Gate not_9 has open pins: in=t_ff_1_q, out=open
  and and_2 (and_2_out, DecSecs, nor_5_out, nor_6_out);
  Multiplexer multiplexer_18 (.in0(and_6_out), .in1(nor_3_out), .out(multiplexer_18_out), .sel(DecMins));
  and and_3 (and_3_out, DecMins, nor_4_out, nor_3_out);
  and and_4 (and_4_out, counter_2_q[0], and_8_out, counter_2_q[2]);
  and and_5 (and_5_out, nor_2_out, DecHrs, nor_1_out);
  and and_6 (and_6_out, counter_5_q[3], multiplexer_20_out, counter_5_q[0]);
  and and_7 (and_7_out, counter_6_q[0], and_6_out, counter_6_q[2]);
  Multiplexer multiplexer_19 (.in0(1'b1), .in1(and_7_out), .out(multiplexer_19_out), .sel(not_11_out));
  and and_8 (and_8_out, counter_1_q[3], multiplexer_19_out, counter_1_q[0]);
  nor nor_1 (nor_1_out, counter_1_q[0], counter_1_q[1], counter_1_q[2], counter_1_q[3]);
  nor nor_2 (nor_2_out, counter_2_q[0], counter_2_q[2], counter_2_q[1]);
  and and_9 (and_9_out, counter_3_q[3], counter_3_q[0]);
  and and_10 (and_10_out, counter_4_q[0], and_9_out, counter_4_q[2]);
  Multiplexer multiplexer_20 (.in0(1'b1), .in1(and_10_out), .out(multiplexer_20_out), .sel(not_11_out));
  nor nor_3 (nor_3_out, counter_5_q[3], counter_5_q[2], counter_5_q[1], counter_5_q[0]);
  nor nor_4 (nor_4_out, counter_6_q[0], counter_6_q[1], counter_6_q[2]);
  not not_10 (not_10_out, Mode);
  nor nor_5 (nor_5_out, counter_3_q[3], counter_3_q[2], counter_3_q[1], counter_3_q[0]);
  nor nor_6 (nor_6_out, counter_4_q[0], counter_4_q[2], counter_4_q[1]);
  and and_11 (and_11_out, multiplexer_19_out, counter_1_q[0], counter_1_q[1]);
  and and_12 (and_12_out, and_11_out, counter_2_q[1]);
  and and_13 (and_13_out, and_12_out, IncHrs);
  T_Flip_Flop t_ff_2 (.T(not_10_out), .clk(not_10_out), .Q(t_ff_2_q));  // open: Qn, reset, preset
  not not_11 (not_11_out, t_ff_2_q);
  // BCD_to_7_Segment_decoder bcd_to_7_segment_decoder_1: pin names not known; wires that end beside it: G2, E2, F2, D2, counter_5_q, A2, C2, B2
  Multiplexer multiplexer_21 (.in0(undriven_2), .in1(undriven_3), .sel(undriven_4));  // open: out
  // BCD_to_7_Segment_decoder bcd_to_7_segment_decoder_2: pin names not known; wires that end beside it: G0, E0, F0, D0, counter_3_q, A0, C0
  // BCD_to_7_Segment_decoder bcd_to_7_segment_decoder_3: pin names not known; wires that end beside it: G3, E3, F3, D3, {1'b0, counter_6_q}, A3, C3, B3
  // BCD_to_7_Segment_decoder bcd_to_7_segment_decoder_4: pin names not known; wires that end beside it: G4, E4, F4, D4, counter_1_q, A4, C4, B4
  // BCD_to_7_Segment_decoder bcd_to_7_segment_decoder_5: pin names not known; wires that end beside it: G1, E1, F1, D1, {1'b0, counter_4_q[2:0]}, A1, C1, B1
  _7_Segment_Display u_7_segment_display_1 (.g(G5), .f(F5), .a(A5), .b(B5), .e(E5), .d(D5), .c(C5));  // open: dp
  _7_Segment_Display u_7_segment_display_2 (.g(G4), .f(F4), .a(A4), .b(B4), .e(E4), .d(D4), .c(C4));  // open: dp
  // BCD_to_7_Segment_decoder bcd_to_7_segment_decoder_6: pin names not known; wires that end beside it: G5, E5, F5, D5, {1'b0, counter_2_q}, A5, C5, B5
  _7_Segment_Display u_7_segment_display_3 (.g(G3), .f(F3), .a(A3), .b(B3), .e(E3), .d(D3), .c(C3));  // open: dp
  _7_Segment_Display u_7_segment_display_4 (.g(G2), .f(F2), .a(A2), .b(B2), .e(E2), .d(D2), .c(C2));  // open: dp
  _7_Segment_Display u_7_segment_display_5 (.g(G1), .f(F1), .a(A1), .b(B1), .e(E1), .d(D1), .c(C1));  // open: dp
  _7_Segment_Display u_7_segment_display_6 (.g(G0), .f(F0), .a(A0), .b(B0), .e(E0), .d(D0), .c(C0));  // open: dp
endmodule
